# Fritzing sketch Prototype1 (saved by Fritzing 0.9.9b)
breadboards: 2

parts:
  Part1 = Arduino Nano (Rev3.0)
  S1 = Round Pushbutton
  Grove1 = Grove Infrared Emitter
  R1 = Resistor [tolerance=±5% resistance=10 package="2010 [SMD]"]
  Joystick = rounded female pin header, 5 pins [form="♀ (female rounded)"]
  R2 = Resistor [tolerance=±5% resistance=10 package="2010 [SMD]"]
  R3 = Resistor [tolerance=±5% resistance=10 package="2010 [SMD]"]
  R4 = Resistor [tolerance=±5% resistance=10 package="2010 [SMD]"]
  R5 = Resistor [tolerance=±5% resistance=10 package="2010 [SMD]"]
  R6 = Resistor [tolerance=±5% resistance=10 package="2010 [SMD]"]
  J2 = rounded female pin header, 2 pins [form="♀ (female rounded)"]
  J3 = rounded female pin header, 2 pins [form="♀ (female rounded)"]

nets:
  GND: Part1.GND, Grove1.GND, R1.Pin_1, R2.Pin_1, R3.Pin_1, R4.Pin_1, R5.Pin_1, R6.Pin_1
  N1: Part1.D2, S1.leg1, R5.Pin_0, J3.pin2
  N2: Part1.D3, Grove1.TX
  N3: Part1.D4, R6.Pin_0, J2.pin2
  N4: Part1.D9, R1.Pin_0, Joystick.pin5
  N5: Part1.D10, Joystick.pin4, R2.Pin_0
  N6: Part1.D11/MOSI, Joystick.pin3, R3.Pin_0
  N7: Part1.D12/MISO, Joystick.pin2, R4.Pin_0
  5V: Part1.5V, S1.leg0, Grove1.VCC, Joystick.pin1, J2.pin1, J3.pin1
