# Fritzing sketch Prototype2Multiplexer (saved by Fritzing 0.9.9b)
breadboards: 2

parts:
  Part1 = Arduino Nano (Rev3.0)
  S1 = Round Pushbutton
  Grove1 = Grove Infrared Emitter
  Joystick = rounded female pin header, 5 pins [form="♀ (female rounded)"]
  R4 = Resistor [tolerance=±5% resistance=10 package="2010 [SMD]"]
  J2 = rounded female pin header, 2 pins [form="♀ (female rounded)"]
  J3 = rounded female pin header, 2 pins [form="♀ (female rounded)"]
  Part2 = Analog Digital MUX Breakout
  J4 = rounded female pin header, 2 pins [form="♀ (female rounded)"]
  J5 = rounded female pin header, 2 pins [form="♀ (female rounded)"]
  J6 = rounded female pin header, 2 pins [form="♀ (female rounded)"]
  J7 = rounded female pin header, 2 pins [form="♀ (female rounded)"]
  J8 = rounded female pin header, 2 pins [form="♀ (female rounded)"]
  J9 = rounded female pin header, 2 pins [form="♀ (female rounded)"]

nets:
  GND: Part1.GND, Grove1.GND, R4.Pin_1, Part2.GND
  N1: Part1.D3, Grove1.TX
  N2: Part1.D4, R4.Pin_0, Part2.SIG
  N3: Part1.D5, Part2.S0
  N4: Part1.D6, Part2.S1
  N5: Part1.D7, Part2.S2
  N6: Part1.D8, Part2.S3
  N7: Part1.D9, Part2.EN
  VCC: Part1.5V, S1.leg0, Grove1.VCC, Joystick.pin1, J2.pin1, J3.pin1, Part2.VCC, J4.pin1, J5.pin1, J6.pin1, J7.pin1, J8.pin1, J9.pin1
  N8: S1.leg1, J3.pin2, Part2.C1
  N9: Joystick.pin2, Part2.C12
  N10: Joystick.pin3, Part2.C13
  N11: Joystick.pin4, Part2.C14
  N12: Joystick.pin5, Part2.C15
  N13: J2.pin2, Part2.C0
  N14: Part2.C2, J4.pin2
  N15: Part2.C3, J5.pin2
  N16: Part2.C4, J6.pin2
  N17: Part2.C5, J8.pin2
  N18: Part2.C6, J7.pin2
  N19: Part2.C7, J9.pin2
