# Fritzing sketch Prototype3MultiplexerBoard (saved by Fritzing 0.9.9b)
breadboards: 2
stripboards: 1

parts:
  Part1 = Arduino Nano (Rev3.0)
  S1 = Round Pushbutton
  Grove1 = Grove Infrared Emitter
  Joystick = rounded female pin header, 5 pins [form="♀ (female rounded)"]
  R4 = Resistor [tolerance=±5% resistance=10 package="2010 [SMD]"]
  J2 = rounded female pin header, 2 pins [form="♀ (female rounded)"]
  J3 = rounded female pin header, 2 pins [form="♀ (female rounded)"]
  J4 = rounded female pin header, 2 pins [form="♀ (female rounded)"]
  J5 = rounded female pin header, 2 pins [form="♀ (female rounded)"]
  J6 = rounded female pin header, 2 pins [form="♀ (female rounded)"]
  J7 = rounded female pin header, 2 pins [form="♀ (female rounded)"]
  J8 = rounded female pin header, 2 pins [form="♀ (female rounded)"]
  J9 = rounded female pin header, 2 pins [form="♀ (female rounded)"]
  Part2 = Analog Digital MUX Breakout  # not connected

nets:
  GND: Part1.GND, Grove1.GND, R4.Pin_0
  N1: Part1.D3, Grove1.TX
  N2: Part1.D4, R4.Pin_1
  5V: Part1.5V, S1.leg1, Grove1.VCC, Joystick.pin1, J2.pin1, J3.pin1, J4.pin1, J5.pin1, J6.pin1, J7.pin1, J8.pin1, J9.pin1
  N3: S1.leg0, J9.pin2
