# Fritzing sketch Prototype4MultiplexerBoardResistors (saved by Fritzing 0.9.9b)
breadboards: 2
stripboards: 1

parts:
  Part1 = Arduino Nano (Rev3.0)
  S1 = Round Pushbutton
  Grove1 = Grove Infrared Emitter
  Joystick = rounded female pin header, 5 pins [form="♀ (female rounded)"]
  R4 = Resistor [tolerance=±5% resistance=10 package="2010 [SMD]"]
  J2 = rounded female pin header, 2 pins [form="♀ (female rounded)"]
  J3 = rounded female pin header, 2 pins [form="♀ (female rounded)"]
  J4 = rounded female pin header, 2 pins [form="♀ (female rounded)"]
  J5 = rounded female pin header, 2 pins [form="♀ (female rounded)"]
  J6 = rounded female pin header, 2 pins [form="♀ (female rounded)"]
  J7 = rounded female pin header, 2 pins [form="♀ (female rounded)"]
  J8 = rounded female pin header, 2 pins [form="♀ (female rounded)"]
  J9 = rounded female pin header, 2 pins [form="♀ (female rounded)"]
  Part2 = Analog Digital MUX Breakout  # not connected
  R5 = Resistor [tolerance=±5% resistance=10 package="2010 [SMD]"]
  R6 = Resistor [tolerance=±5% resistance=10 package="2010 [SMD]"]
  R7 = Resistor [tolerance=±5% resistance=10 package="2010 [SMD]"]
  R8 = Resistor [tolerance=±5% resistance=10 package="2010 [SMD]"]
  R9 = Resistor [tolerance=±5% resistance=10 package="2010 [SMD]"]
  R10 = Resistor [tolerance=±5% resistance=10 package="2010 [SMD]"]
  R11 = Resistor [tolerance=±5% resistance=10 package="2010 [SMD]"]
  R12 = Resistor [tolerance=±5% resistance=10 package="2010 [SMD]"]

nets:
  GND: Part1.GND, Grove1.GND, R4.Pin_0, R5.Pin_0, R6.Pin_0, R7.Pin_0, R8.Pin_0, R9.Pin_0, R10.Pin_0, R11.Pin_0, R12.Pin_0
  N1: Part1.D3, Grove1.TX
  N2: Part1.D4, R4.Pin_1
  5V: Part1.5V, S1.leg1, Grove1.VCC, Joystick.pin1, J2.pin1, J3.pin1, J4.pin1, J5.pin1, J6.pin1, J7.pin1, J8.pin1, J9.pin1
  N3: S1.leg0, J9.pin2, R12.Pin_1
  N4: J2.pin2, R5.Pin_1
  N5: J3.pin2, R9.Pin_1
  N6: J4.pin2, R6.Pin_1
  N7: J5.pin2, R10.Pin_1
  N8: J6.pin2, R7.Pin_1
  N9: J7.pin2, R8.Pin_1
  N10: J8.pin2, R11.Pin_1
