# Fritzing sketch Prototype5MultiplexerBoardResistors (saved by Fritzing 0.9.9b)
breadboards: 2
stripboards: 2

parts:
  Part1 = Arduino Nano (Rev3.0)
  S1 = Round Pushbutton
  Grove1 = Grove Infrared Emitter
  R4 = Resistor [tolerance=±5% resistance=10 package="2010 [SMD]"]
  Part2 = Analog Digital MUX Breakout  # not connected
  J10 = rounded female pin header, 2 pins [form="♀ (female rounded)"]
  R13 = Resistor [tolerance=±5% resistance=10 package="2010 [SMD]"]
  Joystick1 = rounded female pin header, 5 pins [form="♀ (female rounded)"]
  R14 = Resistor [tolerance=±5% resistance=10 package="2010 [SMD]"]
  R15 = Resistor [tolerance=±5% resistance=10 package="2010 [SMD]"]
  R16 = Resistor [tolerance=±5% resistance=10 package="2010 [SMD]"]
  J11 = rounded female pin header, 2 pins [form="♀ (female rounded)"]
  J12 = rounded female pin header, 2 pins [form="♀ (female rounded)"]
  J13 = rounded female pin header, 2 pins [form="♀ (female rounded)"]
  R17 = Resistor [tolerance=±5% resistance=10 package="2010 [SMD]"]
  R20 = Resistor [tolerance=±5% resistance=10 package="2010 [SMD]"]
  R21 = Resistor [tolerance=±5% resistance=10 package="2010 [SMD]"]
  R22 = Resistor [tolerance=±5% resistance=10 package="2010 [SMD]"]
  R23 = Resistor [tolerance=±5% resistance=10 package="2010 [SMD]"]
  J14 = rounded female pin header, 2 pins [form="♀ (female rounded)"]
  R24 = Resistor [tolerance=±5% resistance=10 package="2010 [SMD]"]
  J15 = rounded female pin header, 2 pins [form="♀ (female rounded)"]
  R25 = Resistor [tolerance=±5% resistance=10 package="2010 [SMD]"]
  J16 = rounded female pin header, 2 pins [form="♀ (female rounded)"]
  R26 = Resistor [tolerance=±5% resistance=10 package="2010 [SMD]"]
  J17 = rounded female pin header, 2 pins [form="♀ (female rounded)"]

nets:
  GND: Part1.GND, Grove1.GND, R4.Pin_0, R13.Pin_0, R14.Pin_0, R15.Pin_0, R16.Pin_0, R17.Pin_1, R20.Pin_1, R21.Pin_1, R22.Pin_1, R23.Pin_0, R24.Pin_0, R25.Pin_0, R26.Pin_0
  N1: Part1.D3, Grove1.TX
  N2: Part1.D4, R4.Pin_1
  5V: Part1.5V, S1.leg1, Grove1.VCC, J10.pin1, Joystick1.pin5, J11.pin1, J12.pin1, J13.pin1, J14.pin1, J15.pin1, J16.pin1, J17.pin1
  N3: S1.leg0, R23.Pin_1, J14.pin2
  N4: J10.pin2, R13.Pin_1
  N5: Joystick1.pin1, R17.Pin_0
  N6: Joystick1.pin2, R20.Pin_0
  N7: Joystick1.pin3, R21.Pin_0
  N8: Joystick1.pin4, R22.Pin_0
  N9: R14.Pin_1, J12.pin2
  N10: R15.Pin_1, J13.pin2
  N11: R16.Pin_1, J11.pin2
  N12: R24.Pin_1, J15.pin2
  N13: R25.Pin_1, J16.pin2
  N14: R26.Pin_1, J17.pin2
