# Fritzing sketch Prototype6 (saved by Fritzing 0.9.9b)
breadboards: 2

parts:
  Part1 = Arduino Nano (Rev3.0)
  S1 = Round Pushbutton  # not connected
  Grove1 = Grove Infrared Emitter
  R4 = Resistor [tolerance=±5% resistance=10 package="2010 [SMD]"]
  Part2 = Analog Digital MUX Breakout  # not connected
  Joystick = rounded female pin header, 5 pins [form="♀ (female rounded)"]
  S2 = Round Pushbutton  # not connected
  S3 = Round Pushbutton
  Part3 = Analog Digital MUX Breakout  # not connected
  CONN1 = USB connector [package=THT]
  USB_Power = rounded female pin header, 4 pins [form="♀ (female rounded)"]
  S4 = Taiway 100-SP-X-T1 SPDT Miniature Toggle Switch [part_number=100-SP-X-T1-0-0-B1-M2 package=THT]

nets:
  GND: Part1.GND, Grove1.GND, R4.Pin_0, CONN1.GND, CONN1.chassis5, CONN1.chassis6, USB_Power.pin4
  N1: Part1.D3, Grove1.TX
  N2: Part1.D4, R4.Pin_1
  5V: Part1.5V, Grove1.VCC, Joystick.pin5, S3.leg0, S4.COM
  N3: CONN1.5V, USB_Power.pin1, S4.L1

notes:
  ...
